# Fritzing sketch bluetooth (saved by Fritzing 0.8.5b)
circuit board: 8.91243cm x 7.15428cm
breadboards: 1

parts:
  XTAL1 = Crystal [frequency="16 MHz" package=SMD]
  Parte3 = Bluetooth Mate Silver
  C1 = Ceramic Capacitor [capacitance=12pF package="100 mil [THT, multilayer]"]
  S1 = Pushbutton [package=THT]
  U3 = atmega328 [package=dip]
  C2 = Ceramic Capacitor [capacitance=12pF package="100 mil [THT, multilayer]"]
  R1 = Resistor [tolerance=±5% resistance=500 package=THT]
  VCC1 = 4 x AAA Battery Mount

nets (from the pcb view):
  N1: XTAL1.pin_0, U3.GND#7, U3.XLAT1, C2.0
  N2: XTAL1.pin_1, C1.1, U3.XLAT2
  N3: Parte3.RX_5V, U3.D1_(TX)
  N4: Parte3.TX_5V, U3.D0_(RX)
  VCC: Parte3.VCC, U3.VCC, U3.AVCC, VCC1.+
  N5: Parte3.GND, C1.0, U3.GND#21, C2.1, R1.Pin_0, VCC1.-
  N6: S1.leg0, U3.RESET
  N7: S1.leg1, R1.Pin_1

notes:
  modulo bluetooth
