# Fritzing sketch diodosled (saved by Fritzing 0.8.5b)
breadboards: 1

parts:
  U3 = atmega328 [package=dip]
  LED2 = LED - 5mm [color="Infrared (940nm)" package="5 mm [THT]"]
  LED3 = LED - 5mm [color="Infrared (850nm)" package="5 mm [THT]"]
  R1 = Resistor [tolerance=±5% resistance=1k package=THT]
  R3 = Resistor [tolerance=±5% resistance=220 package=THT]
  R2 = Resistor [tolerance=±5% resistance=1k package=THT]
  LED1 = LED - 5mm [color="Infrared (940nm)" package="5 mm [THT]"]

nets (from the schematic view):
  5V: U3.VCC, U3.AVCC, LED2.anode, LED1.anode
  GND: U3.GND, R1.Pin_1, R3.Pin_0, R2.Pin_0
  N1: U3.D6_(PWM), LED3.cathode
  N2: U3.A0, R2.Pin_1, LED1.cathode
  N3: U3.A5, LED2.cathode, R3.Pin_1
  N4: LED3.anode, R1.Pin_0
