# Fritzing sketch motor (saved by Fritzing 0.8.5b)
breadboards: 1

parts:
  U2 = mystery part, 3 pins [chip_label=tip122]
  D2 = Rectifier Diode [part_number=1N4001 package="300 mil [THT]"]
  M2 = DC Motor
  C2 = Ceramic Capacitor [capacitance=12pF package="100 mil [THT, multilayer]"]
  U3 = atmega328 [package=dip]
  R1 = Resistor [tolerance=±5% resistance=1k package=THT]

nets (from the schematic view):
  N1: U2.pin1, R1.Pin_1
  5V: U2.pin2, D2.cathode, U3.VCC, U3.AVCC
  GND: U2.pin3, M2.pin_1, C2.0, U3.GND
  N2: D2.anode, M2.pin_2, C2.1
  N3: U3.D3_(PWM), R1.Pin_0
