# Fritzing sketch rgb (saved by Fritzing 0.8.5b)
circuit board: 8.46667cm x 5.64444cm
breadboards: 1

parts:
  U3 = atmega328 [package=dip]
  LED1 = RGB LED (com. anode, rbg) [package="5 mm [THT]"]
  R2 = Resistor [tolerance=±5% resistance=500 package=THT]
  R3 = Resistor [tolerance=±5% resistance=500 package=THT]
  R1 = Resistor [tolerance=±5% resistance=500 package=THT]

nets (from the pcb view):
  N1: U3.D9_(PWM), R2.Pin_1
  N2: U3.D10_(PWM), R3.Pin_1
  N3: U3.D12, R1.Pin_1
  N4: U3.AVCC, LED1.common_anode
  N5: LED1.red_cathode, R1.Pin_0
  N6: LED1.blue_cathode, R3.Pin_0
  N7: LED1.green_cathode, R2.Pin_0
