# Fritzing sketch sensores3 (saved by Fritzing 0.8.5b)
breadboards: 2

parts:
  D1 = Rectifier Diode [part_number=1N4001 package="300 mil [THT]"]
  R1 = Resistor [tolerance=±5% resistance=1k package=THT]
  M1 = DC Motor
  LED1 = smd LED [color="Infrared (940nm)" package="1206 [SMD]"]
  LED2 = smd LED [color="Infrared (940nm)" package="1206 [SMD]"]
  LED3 = RGB LED (com. anode, rbg) [package="5 mm [THT]"]
  C1 = Ceramic Capacitor [capacitance=100nF package="100 mil [THT, multilayer]"]
  R4 = Resistor [tolerance=±5% resistance=1k package=THT]
  R5 = Resistor [tolerance=±5% resistance=1k package=THT]
  R6 = Resistor [tolerance=±5% resistance=220 package=THT]
  R7 = Resistor [tolerance=±5% resistance=220 package=THT]
  R8 = Resistor [tolerance=±5% resistance=220 package=THT]
  U1 = mystery part, 3 pins [chip_label=tip122]
  LED4 = smd LED [color="Infrared (850nm)" package="1206 [SMD]"]
  R9 = Resistor [tolerance=±5% resistance=500 package=THT]
  U2 = atmega328 [package=dip]
  XTAL1 = Crystal [frequency="16 MHz" package=THT]
  C3 = Ceramic Capacitor [capacitance=100nF package="100 mil [THT, multilayer]"]
  C4 = Ceramic Capacitor [capacitance=100nF package="100 mil [THT, multilayer]"]
  Parte1 = Bluetooth Module Breakout - Roving Networks (RN-41)

nets (from the schematic view):
  5V: D1.cathode, LED1.anode, LED2.anode, LED3.common_anode, U1.pin2, U2.VCC, U2.AREF, Parte1.VCC
  N1: R1.Pin_0, U1.pin1
  N2: R1.Pin_1, U2.D3_(PWM)
  N3: M1.pin_1, C1.0, U1.pin3
  GND: M1.pin_2, C1.1, R4.Pin_1, R5.Pin_1, R9.Pin_0, U2.GND, C3.1, C4.1, Parte1.GND
  N4: LED1.cathode, R5.Pin_0, U2.A1
  N5: LED2.cathode, R4.Pin_0, U2.A0
  N6: LED3.red_cathode, R6.Pin_0
  N7: LED3.blue_cathode, R8.Pin_0
  N8: LED3.green_cathode, R7.Pin_0
  N9: R6.Pin_1, U2.D12
  N10: R7.Pin_1, U2.D10_(PWM)
  N11: R8.Pin_1, U2.D9_(PWM)
  N12: LED4.cathode, U2.D13
  N13: LED4.anode, R9.Pin_1
  N14: U2.D0_(RX), Parte1.UARTTX
  N15: U2.D1_(TX), Parte1.UARTRX
  N16: U2.XLAT1, XTAL1.pin_1, C3.0
  N17: U2.XLAT2, XTAL1.pin_0, C4.0

notes:
  A0
  3
  A1
  D12
  D10
  D9
  Diego Alberto Parra Garzón
  Colombia, Bogotá
  Montaje de sensores
  Tip122 "CVM"
  diodo RGB "I"
  Motor "VM"
  diodo "IRR1"
  diodo "IRR2"
  diodo "IRE2"
  D13
