# Fritzing sketch sensores3 (saved by Fritzing 0.8.5b)
circuit board: 17.3743cm x 8.32402cm
breadboards: 3

parts:
  D1 = Rectifier Diode [part_number=1N4001 package="300 mil [THT]"]
  R1 = Resistor [tolerance=±10% resistance=1k package=THT]
  M1 = DC Motor
  LED1 = smd LED [color="Infrared (940nm)" package="1206 [SMD]"]
  LED2 = smd LED [color="Infrared (940nm)" package="1206 [SMD]"]
  C1 = Ceramic Capacitor [capacitance=100nF package="100 mil [THT, multilayer]"]
  R4 = Resistor [tolerance=±5% resistance=1k package=THT]
  R5 = Resistor [tolerance=±5% resistance=1k package=THT]
  R6 = Resistor [tolerance=±5% resistance=220 package=THT]
  R7 = Resistor [tolerance=±5% resistance=220 package=THT]
  R8 = Resistor [tolerance=±5% resistance=220 package=THT]
  LED4 = smd LED [color="Infrared (850nm)" package="1206 [SMD]"]
  R9 = Resistor [tolerance=±5% resistance=500 package=THT]
  U2 = atmega328 [package=dip]
  XTAL1 = Crystal [frequency="16 MHz" package=THT]
  C3 = Ceramic Capacitor [capacitance=10pF voltage=20V package="100 mil [THT, multilayer]"]
  C4 = Ceramic Capacitor [capacitance=10pF package="200 mil [THT, multilayer]"]
  Q1 = Basic FET P-Channel [package="TO220 [THT]"]
  C6 = Electrolytic Capacitor [capacitance=10µF package="100 mil [THT, electrolytic]"]
  VCC1 = Battery block 9V
  C7 = Electrolytic Capacitor [capacitance=10µF package="100 mil [THT, electrolytic]"]
  S1 = Pushbutton [package=THT]
  R10 = Resistor [tolerance=±5% resistance=500 package=THT]
  Parte2 = Bluetooth Mate Silver
  U1 = mystery part, 3 pins [chip_label=tip122]
  LED3 = RGB LED (com. anode, rbg) [package="5 mm [THT]"]

nets (from the pcb view):
  N1: D1.cathode, M1.pin_1, C1.0, U1.pin3
  N2: D1.anode, M1.pin_2, C1.1, R9.Pin_1, U2.AVCC, U1.pin2, LED3.common_anode
  N3: R1.Pin_0, U1.pin1
  N4: R1.Pin_1, U2.D3_(PWM)
  N5: LED1.cathode, R5.Pin_1, U2.A5
  N6: LED2.cathode, R4.Pin_1
  N7: LED2.anode, U2.D6_(PWM)
  N8: R4.Pin_0, R5.Pin_0, U2.GND#7, C3.0, C4.0, Q1.drain, C6.-, VCC1.-, C7.-, R10.Pin_0, Parte2.GND
  N9: R6.Pin_0, LED3.blue_cathode
  N10: R6.Pin_1, U2.D10_(PWM)
  N11: R7.Pin_0, LED3.green_cathode
  N12: R7.Pin_1, U2.D9_(PWM)
  N13: R8.Pin_0, LED3.red_cathode
  N14: R8.Pin_1, U2.D12
  N15: LED4.cathode, R9.Pin_0, U2.A0
  N16: U2.RESET, S1.leg0
  N17: U2.D0_(RX), Parte2.TX_5V
  N18: U2.D1_(TX), Parte2.RX_5V
  VCC: U2.VCC, Q1.gate, C6.+, Parte2.VCC
  N19: U2.XLAT1, XTAL1.pin_0, C3.1
  N20: U2.XLAT2, XTAL1.pin_1, C4.1
  N21: Q1.source, VCC1.+, C7.+
  N22: S1.leg1, R10.Pin_1

notes:
  A0
  3
  A1
  D12
  D10
  D9
  Diego Alberto Parra Garzón
  Colombia, Bogotá
  Montaje experimental
  Tip122 "CVM"
  diodo RGB "I"
  Motor "VM"
  diodo "IRR1"
  diodo "IRR2"
  diodo "IRE2"
  D13
  lm 7805cv
  Bogotá. Colombia
