# Fritzing sketch tareaf electronica (saved by Fritzing 0.8.5b)
breadboards: 1

parts:
  V1 = DC Power [voltage=110]
  R1 = Resistor [tolerance=±5% resistance=220 package=THT]
  S1 = Pushbutton [package=THT]
  R2 = Resistor [tolerance=±5% resistance=220 package=THT]
  S2 = Pushbutton [package=THT]
  R3 = Resistor [tolerance=±5% resistance=220 package=THT]
  R4 = Resistor [tolerance=±5% resistance=220 package=THT]
  S3 = Pushbutton [package=THT]
  R5 = Resistor [tolerance=±5% resistance=220 package=THT]
  M1 = DC Motor
  S4 = Pushbutton [package=THT]
  S5 = Pushbutton [package=THT]
  R6 = Resistor [tolerance=±5% resistance=220 package=THT]
  M2 = DC Motor
  R7 = Resistor [tolerance=±5% resistance=220 package=THT]
  S6 = Pushbutton [package=THT]
  R8 = Resistor [tolerance=±5% resistance=220 package=THT]
  S7 = Pushbutton [package=THT]
  M3 = DC Motor
  S8 = Pushbutton [package=THT]
  R9 = Resistor [tolerance=±5% resistance=220 package=THT]
  S9 = Pushbutton [package=THT]

nets:
  N1: V1.V+, R1.Pin_0, R2.Pin_0, S4.leg0, R7.Pin_1, S9.leg0
  N2: V1.V-, S1.leg1, R3.Pin_0, S3.leg1, M1.pin_2, M2.pin_2, S6.leg1, R8.Pin_1, M3.pin_1, R9.Pin_1
  N3: R2.Pin_1, S2.leg0
  N4: R3.Pin_1, R4.Pin_0
  N5: R4.Pin_1, S3.leg0
  N6: R5.Pin_1, M1.pin_1
  N7: S5.leg0, S7.leg0, S8.leg0
  N8: R6.Pin_1, M2.pin_1
  N9: R7.Pin_0, S6.leg0
  N10: R8.Pin_0, S7.leg1
  N11: M3.pin_2, S8.leg1
  N12: R9.Pin_0, S9.leg1

notes:
  HABITACIÓN 1 Y 2
  SALA COMEDOR
  BAÑOS
  ESTUDIO
  COCINA
  LAVANDERIA
  DIEGO ALBERTO PARRA GARZÓN
