# Fritzing sketch transformador 5V (saved by Fritzing 0.8.5b)
circuit board: 6.34512cm x 3.24809cm
breadboards: 1

parts:
  C1 = Electrolytic Capacitor [capacitance=10µF package="100 mil [THT, electrolytic]"]
  C2 = Electrolytic Capacitor [capacitance=10µF package="100 mil [THT, electrolytic]"]
  U1 = Voltage Regulator - 5V [package="TO220 [THT]"]
  VCC1 = Battery block 9V
  Power_plug1 = Power plug

nets:
  GND: C1.-, C2.-, U1.GND, VCC1.-, Power_plug1.GND
  N1: C1.+, U1.input_voltage, VCC1.+
  N2: C2.+, U1.output_voltage, Power_plug1.VCC

notes:
  lm 7806 cv
  condensadores
  electroliticos
  bateria 9 V
  Diego Alberto Parra
  Transformador de 9V a 5V
